# Fritzing sketch Sketch (saved by Fritzing 0.9.3b)

parts:
  Componente1 = Arduino Nano (Rev3.0)
  S1 = Momentary Switch [package=ksa_sealed_tac_switch]
  LED1 = LED - 5mm [color="Red (633nm)" package="5 mm [THT]"]
  LED2 = LED - 5mm [color="Red (633nm)" package="5 mm [THT]"]
  R2 = Resistor [tolerance=±5% resistance=220 package="2010 [SMD]"]
  R1 = Photocell (LDR) [package=THT]
  R3 = Resistor [tolerance=±5% resistance=220 package="2010 [SMD]"]

nets:
  N1: Componente1.GND, LED1.anode, R3.Pin_0
  N2: Componente1.D2, LED1.cathode
  N3: Componente1.D6, S1.2, R3.Pin_1
  N4: Componente1.D7, S1.4
  N5: Componente1.D10, LED2.anode
  N6: Componente1.D11/MOSI, LED2.cathode
  N7: Componente1.5V, R2.Pin_0
  N8: Componente1.A4, R2.Pin_1, R1.pin_0
  N9: Componente1.D13/SCK, R1.pin_1
